# Fritzing sketch game (saved by Fritzing 0.7.12b)
breadboards: 1

parts:
  Arduino1 = Arduino
  LED1 = LED - 5mm [color="Red (633nm)" package="5 mm [THT]"]
  LED2 = LED - 5mm [color="Green (555nm)" package="5 mm [THT]"]
  LED3 = LED - 5mm [color="Yellow (595nm)" package="5 mm [THT]"]
  LED4 = LED - 5mm [color="White (8000K)" package="5 mm [THT]"]
  R1 = Resistor [tolerance=±5% resistance=330 package=THT]
  R2 = Resistor [tolerance=±5% resistance=330 package=THT]
  R3 = Resistor [tolerance=±5% resistance=330 package=THT]
  R4 = Resistor [tolerance=±5% resistance=330 package=THT]
  S1 = Pushbutton [package="[THT]"]
  R5 = Resistor [tolerance=±5% resistance=220 package=THT]

nets:
  N1: Arduino1.GND, LED1.cathode, LED2.cathode, LED3.cathode, LED4.cathode, S1.Pin_1, S1.Pin_2
  N2: Arduino1.D13, S1.Pin_3, S1.Pin_4, R5.Pin_1
  N3: Arduino1.D5, R1.Pin_1
  N4: Arduino1.D4, R2.Pin_1
  N5: Arduino1.D3, R3.Pin_1
  N6: Arduino1.D2, R4.Pin_1
  N7: Arduino1.+5V, R5.Pin_0
  N8: LED1.anode, R1.Pin_0
  N9: LED2.anode, R2.Pin_0
  N10: LED3.anode, R3.Pin_0
  N11: LED4.anode, R4.Pin_0
