# Fritzing sketch inputs (saved by Fritzing 0.7.12b)
breadboards: 1

parts:
  Arduino1 = Arduino
  S1 = Pushbutton [package="[THT]"]
  R1 = Resistor [tolerance=±5% resistance=10k package=THT]

nets:
  N1: Arduino1.D13, S1.Pin_3, S1.Pin_4, R1.Pin_1
  N2: Arduino1.+5V, R1.Pin_0
  N3: Arduino1.GND, S1.Pin_1, S1.Pin_2
